# Fritzing sketch env_data (saved by Fritzing 0.9.9b)
perfboards: 1

parts:
  Part1 = Arduino Nano 33 IOT
  Part2 = Adafruit CCS811
  RHT1 = Humidity and Temperature Sensor RHT03
  S1 = Pushbutton [package="[THT]"]
  J1 = male pin header, 4 pins [form="♂ (male)"]
  J2 = male pin header, 1 pin [form="♂ (male)"]  # not connected
  J3 = male pin header, 2 pins [form="♂ (male)"]
  J4 = male pin header, 2 pins [form="♂ (male)"]
  R1 = Resistor [tolerance=±5% power=0.25 resistance=10k package=THT]
  R2 = Resistor [tolerance=±5% power=0.25 resistance=100 package=THT]
  R3 = Resistor [tolerance=±5% power=0.25 resistance=330 package=THT]

nets:
  N1: Part1.RESET, Part1.A7, J1.pin4
  N2: Part1.GND, Part1.D13~, RHT1.GND_2, S1.Pin_3, S1.Pin_4, J1.pin2, J3.pin1
  N3: Part1.D7, RHT1.Data-signal, R1.Pin_1
  N4: Part1.D8, S1.Pin_1, S1.Pin_2
  N5: Part1.D11/MOSI, Part1.+5V
  N6: Part1.VIN, J1.pin1
  N7: Part1.A6, R2.Pin_1
  N8: Part1.A5, Part2.SDA
  N9: Part1.A4, Part2.SCL
  N10: Part1.A1, Part2.!WAKE
  N11: Part1.A0, Part2.!INT
  3V3: Part1.3V3, Part2.VIN
  N12: Part2.GND, R3.Pin_1
  N13: RHT1.Vcc, R1.Pin_0
  N14: J1.pin3, J4.pin2, R2.Pin_0
  N15: J3.pin2, J4.pin1

custom parts:
  Arduino Nano 33 IOT: The Arduino Nano 33 IoT is the easiest and cheapest point of entry to enhance existing devices (and creating new ones) to be part of the IoT and designing pico-network applications. Whether you are looking at building a sensor network connected to your office or home router, or if you want to create a BLE device sending data to a cellphone, the Nano 33 IoT is your one-stop-solution for many of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
